// Logisim project logisim elevador.circ as structural Verilog: 8 circuits, main circuit main
module main (
);

  wire and_1_out, clock_1_out, clock_2_out, clock_3_out, comparator_1_eq, comparator_2_eq, F0_out, F1_out,
       F2_out, F3_out, F4_out, segment_a_1_out_2, segment_b_1_out_2, segment_c_1_out_2, segment_d_1_out_2,
       segment_e_1_out_2, segment_f_1_out_2, segment_g_1_out_2;
  wire [3:0] adder_1_out, multiplexer_1_out, multiplexer_2_out, register_1_q, register_2_q, register_3_q,
       subtractor_1_out;
  wire [4:0] t_ff_5_q;
  wire [6:0] undriven, undriven_2, undriven_3, undriven_4, undriven_5, undriven_6;
  wire [6:6] or_2_out;

  Button F4 (.out(F4_out));
  Button F3 (.out(F3_out));
  Button F2 (.out(F2_out));
  Button F1 (.out(F1_out));
  Button F0 (.out(F0_out));
  T_Flip_Flop t_ff_1 (.clk(F4_out), .T(F4_out), .Q(t_ff_5_q[4]), .reset(comparator_1_eq));  // open: Qn, preset, en
  T_Flip_Flop t_ff_2 (.clk(F3_out), .T(F3_out), .Q(t_ff_5_q[3]), .reset(comparator_1_eq));  // open: Qn, preset, en
  T_Flip_Flop t_ff_3 (.clk(F2_out), .T(F2_out), .Q(t_ff_5_q[2]), .reset(comparator_1_eq));  // open: Qn, preset, en
  T_Flip_Flop t_ff_4 (.clk(F1_out), .T(F1_out), .Q(t_ff_5_q[1]), .reset(comparator_1_eq));  // open: Qn, preset, en
  T_Flip_Flop t_ff_5 (.clk(F0_out), .T(F0_out), .Q(t_ff_5_q[0]), .reset(comparator_1_eq));  // open: Qn, preset, en
  Multiplexer #(.select(5), .width(4), .enable("false")) multiplexer_1 (
    .in1(4'b0000), .in2(4'b0001), .in4(4'b0010), .in8(4'b0011), .in16(4'b0100), .out(multiplexer_1_out),
    .sel(t_ff_5_q));  // open: in0, in3, in5, in6, in7, in9, in10, in11, in12, in13, in14, in15, in17, in18, in19, in20, in21, in22, in23, in24, in25, in26, in27, in28, in29, in30, in31
  Comparator #(.width(4)) comparator_1 (
    .a(register_1_q), .b(multiplexer_1_out), .gt(undriven_2[2]), .eq(comparator_1_eq), .lt(undriven_2[4]));
  Register #(.width(4)) register_1 (.D(multiplexer_2_out), .Q(register_1_q), .clk(clock_1_out));  // open: en, clr
  Clock #(.lowDuration(1000)) clock_1 (.out(clock_1_out));
  Register #(.width(4)) register_2 (.D(multiplexer_2_out), .Q(register_2_q), .clk(clock_2_out));  // open: en, clr
  Clock #(.lowDuration(1000)) clock_2 (.out(clock_2_out));
  Multiplexer #(.width(4), .enable("false")) multiplexer_2 (
    .in0(adder_1_out), .in1(subtractor_1_out), .out(multiplexer_2_out), .sel(undriven_2[2]));
  Adder #(.width(4)) adder_1 (.a(register_2_q), .b(4'b0001), .out(adder_1_out));  // open: cin, cout
  Subtractor #(.width(4)) subtractor_1 (.a(register_2_q), .b(4'b0001), .out(subtractor_1_out));  // open: bin, bout
  Comparator #(.width(4)) comparator_2 (.a(register_1_q), .b(register_3_q), .eq(comparator_2_eq));  // open: gt, lt
  Register #(.width(4)) register_3 (.D(multiplexer_2_out), .Q(register_3_q), .clk(clock_3_out));  // open: en, clr
  Clock #(.lowDuration(1000)) clock_3 (.out(clock_3_out));
  buf and_1 (and_1_out, comparator_2_eq);  // AND_Gate
  segment_a segment_a_1 (.in_1(register_3_q), .out_2(segment_a_1_out_2));
  _7_Segment_Display u_7_segment_display_1 (
    .g(segment_g_1_out_2), .f(segment_f_1_out_2), .a(segment_a_1_out_2), .b(segment_b_1_out_2),
    .e(segment_e_1_out_2), .d(segment_d_1_out_2), .c(segment_c_1_out_2));  // open: dp
  segment_b segment_b_1 (.in_1(register_3_q), .out_2(segment_b_1_out_2));
  segment_c segment_c_1 (.in_1(register_3_q), .out_2(segment_c_1_out_2));
  segment_d segment_d_1 (.in_1(register_3_q), .out_2(segment_d_1_out_2));
  segment_e segment_e_1 (.in_1(register_3_q), .out_2(segment_e_1_out_2));
  segment_f segment_f_1 (.in_1(register_3_q), .out_2(segment_f_1_out_2));
  segment_g segment_g_1 (.in_1(register_3_q), .out_2(segment_g_1_out_2));
  or or_1 (undriven[3], undriven_2[4], undriven_2[2]);
  or or_2 (or_2_out[6], undriven_2[2], undriven_2[4], and_1_out);
  or or_3 (undriven_6[3], undriven_2[4], undriven_2[2]);
  DotMatrix #(.matrixcols(7)) dotmatrix_1 (
    .col0(undriven), .col1(undriven_2),
    .col2({undriven_3[6], undriven_2[4], undriven_3[4:2], undriven_2[2], undriven_3[0]}),
    .col3({7{or_2_out[6]}}),
    .col4({undriven_4[6], undriven_2[4], undriven_4[4:2], undriven_2[2], undriven_4[0]}),
    .col5({undriven_5[6:5], undriven_2[4], undriven_5[3], undriven_2[2], undriven_5[1:0]}), .col6(undriven_6));

  // Notes on the sheet:
  //   abrir
  //   descer
  //   subir
endmodule

module segment_a (
  input  [3:0] in_1,
  output out_2
);

  wire and_1_out, and_2_out, not_1_out, not_2_out, not_3_out, not_4_out, not_5_out;

  and and_1 (and_1_out, in_1[1], not_1_out);
  not not_1 (not_1_out, in_1[3]);
  not not_2 (not_2_out, in_1[3]);
  not not_3 (not_3_out, in_1[2]);
  not not_4 (not_4_out, in_1[1]);
  not not_5 (not_5_out, in_1[0]);
  and and_2 (and_2_out, not_2_out, not_3_out, not_4_out, not_5_out);
  or or_1 (out_2, and_1_out, and_2_out);
endmodule

module segment_b (
  input  [3:0] in_1,
  output out_2
);

  wire not_1_out;

  not not_1 (not_1_out, in_1[3]);
  or or_1 (out_2, in_1[3], not_1_out);
endmodule

module segment_c (
  input  [3:0] in_1,
  output out_2
);

  wire and_1_out, and_2_out, and_3_out, not_1_out, not_2_out, not_3_out, not_4_out, not_5_out;

  not not_1 (not_1_out, in_1[3]);
  not not_2 (not_2_out, in_1[3]);
  not not_3 (not_3_out, in_1[2]);
  not not_4 (not_4_out, in_1[1]);
  not not_5 (not_5_out, in_1[0]);
  and and_1 (and_1_out, in_1[2], not_1_out);
  and and_2 (and_2_out, in_1[0], not_1_out);
  and and_3 (and_3_out, not_2_out, not_3_out, not_4_out, not_5_out);
  or or_1 (out_2, and_1_out, and_2_out, and_3_out);
endmodule

module segment_d (
  input  [3:0] in_1,
  output out_2
);

  wire and_1_out, and_2_out, not_1_out, not_2_out, not_3_out, not_4_out, not_5_out;

  and and_1 (and_1_out, in_1[1], not_1_out);
  not not_1 (not_1_out, in_1[3]);
  not not_2 (not_2_out, in_1[3]);
  not not_3 (not_3_out, in_1[2]);
  not not_4 (not_4_out, in_1[1]);
  not not_5 (not_5_out, in_1[0]);
  and and_2 (and_2_out, not_2_out, not_3_out, not_4_out, not_5_out);
  or or_1 (out_2, and_1_out, and_2_out);
endmodule

module segment_e (
  input  [3:0] in_1,
  output out_2
);

  wire and_1_out, and_2_out, not_1_out, not_2_out, not_3_out, not_4_out, not_5_out, not_6_out, not_7_out;

  not not_1 (not_1_out, in_1[0]);
  not not_2 (not_2_out, in_1[2]);
  not not_3 (not_3_out, in_1[3]);
  not not_4 (not_4_out, in_1[3]);
  not not_5 (not_5_out, in_1[2]);
  not not_6 (not_6_out, in_1[1]);
  not not_7 (not_7_out, in_1[0]);
  and and_1 (and_1_out, not_1_out, in_1[1], not_2_out, not_3_out);
  and and_2 (and_2_out, not_4_out, not_5_out, not_6_out, not_7_out);
  or or_1 (out_2, and_1_out, and_2_out);
endmodule

module segment_f (
  input  [3:0] in_1,
  output out_2
);

  wire and_1_out, and_2_out, not_1_out, not_2_out, not_3_out, not_4_out, not_5_out;

  not not_1 (not_1_out, in_1[3]);
  not not_2 (not_2_out, in_1[3]);
  not not_3 (not_3_out, in_1[2]);
  not not_4 (not_4_out, in_1[1]);
  not not_5 (not_5_out, in_1[0]);
  and and_1 (and_1_out, in_1[2], not_1_out);
  and and_2 (and_2_out, not_2_out, not_3_out, not_4_out, not_5_out);
  or or_1 (out_2, and_1_out, and_2_out);
endmodule

module segment_g (
  input  [3:0] in_1,
  output out_2
);

  wire and_1_out, and_2_out, not_1_out;

  not not_1 (not_1_out, in_1[3]);
  and and_1 (and_1_out, in_1[1], not_1_out);
  and and_2 (and_2_out, in_1[2], not_1_out);
  or or_1 (out_2, and_1_out, and_2_out);
endmodule
